# Fritzing sketch ControlPanel (saved by Fritzing 0.9.0b)
breadboards: 1

parts:
  U1 = MAX7219 [package=dil24]  # not connected
  U2 = MAX7219 [package=dil24]  # not connected
  U3 = MAX7219 [package=dil24]  # not connected
  Raspberry_Pi_3 = Raspberry Pi 3
  S1 = Toggle Switch [package=THT]
  S2 = Toggle Switch [package=THT]
  S3 = Toggle Switch [package=THT]

nets:
  3V3: Raspberry_Pi_3.3v3, Raspberry_Pi_3.3V3, S1.COM, S2.COM, S3.COM
  N1: Raspberry_Pi_3.GIPO25, S1.L2
  N2: Raspberry_Pi_3.GIPO24, S2.L2
  N3: Raspberry_Pi_3.GIPO23, S3.L2
